// Logisim project cpu.circ as structural Verilog: 1 circuit, main circuit cpu
module cpu (
  input  clk,
  input  [31:0] INSTRUCTION,
  input  [31:0] READ_DATA,
  output [31:0] WRITE_ADDRESS,
  output [31:0] PROGRAM_COUNTER,
  output [31:0] ra,
  output [31:0] sp,
  output [31:0] t0,
  output [31:0] t1,
  output [31:0] t2,
  output [31:0] s0,
  output [31:0] s1,
  output [31:0] a0,
  output [31:0] tohost,
  output [3:0] WRITE_ENABLE,
  output [31:0] WRITE_DATA
);

  wire ASel, BrEq, BrLt, BrUn, BSel, CSRSel, CSRWen, MemRW, PCSel, RegWEn;
  wire [1:0] WBSel;
  wire [2:0] immSel;
  wire [3:0] ALUSel;
  wire [31:0] adder_1_out, ALUResult, imm, INSTRUCTION_Fetch, multiplexer_1_out, multiplexer_2_out, rs1, WB;

  Adder #(.width(32)) adder_1 (.a(PROGRAM_COUNTER), .b(32'h4), .out(adder_1_out));  // open: cin, cout
  Register #(.width(32)) PC (.D(adder_1_out), .en(1'b1), .clk(clk), .Q(PROGRAM_COUNTER));  // open: clr
  Register #(.width(32)) register_1 (.D(INSTRUCTION), .en(1'b1), .clk(clk), .Q(INSTRUCTION_Fetch));  // open: clr
  control_logic control_logic_1 (
    .CSRWen(CSRWen), .PCSel(PCSel), .RegWEn(RegWEn), .ImmSel(immSel), .BrUn(BrUn), .ASel(ASel), .BSel(BSel),
    .ALUSel(ALUSel), .MemRW(MemRW), .WBSel(WBSel), .CSRSel(CSRSel), .inst(INSTRUCTION_Fetch), .BrEq(BrEq),
    .BrLt(BrLt));
  imm_gen imm_gen_1 (.inst(INSTRUCTION_Fetch), .ImmSel(immSel), .imm(imm));
  regfile regfile_1 (
    .rs1(INSTRUCTION_Fetch[19:15]), .rs2(INSTRUCTION_Fetch[24:20]), .rd(INSTRUCTION_Fetch[11:7]),
    .Write_Data(WB), .RegWEn(RegWEn), .clk(clk), .ra(ra), .sp(sp), .t0(t0), .t1(t1), .t2(t2), .s0(s0),
    .s1(s1), .a0(a0), .Read_Data_1(rs1), .Read_Data_2(WRITE_DATA));
  branch_comp branch_comp_1 (.rs1(rs1), .rs2(WRITE_DATA), .BrUn(BrUn), .BrEq(BrEq), .BrLt(BrLt));
  Multiplexer #(.enable("false"), .width(32)) multiplexer_1 (
    .in0(rs1), .in1(PROGRAM_COUNTER), .out(multiplexer_1_out), .sel(ASel));
  Multiplexer #(.enable("false"), .width(32)) multiplexer_2 (
    .in0(WRITE_DATA), .in1(imm), .out(multiplexer_2_out), .sel(BSel));
  alu alu_1 (.Result(ALUResult), .A(multiplexer_1_out), .B(multiplexer_2_out), .ALUSel(ALUSel));  // open: out_5
  csr csr_1 (.CSR_WE(CSRWen), .clk(clk), .tohost(tohost));  // open: CSR_address, CSR_din
  Multiplexer #(.enable("false"), .select(2), .width(32)) multiplexer_3 (
    .in0(ALUResult), .in1(READ_DATA), .out(WB), .sel(WBSel));  // open: in2, in3

  // Other names for the same wires on the sheet: rs2[31:0] = WRITE_DATA

  // Notes on the sheet:
  //   Output to IMEM
  //   IMEM (do **NOT** move this)
  //   Inputs from IMEM
  //   Inputs/Outputs for testing. Do **NOT** move these.
  //   Outputs To DMEM
  //   DMEM (do **NOT** move this)
  //   Inputs From DMEM
endmodule
